// Logisim project Lucas_Neves_SI4N.circ as structural Verilog: 16 circuits, main circuit ULA
module main (
);

  wire clock_1_out, d_ff_1_q, not_1_out, not_2_out, Overflow_q, Reset_out, uc_1_ac, uc_1_e, uc_1_ir,
       uc_1_load, uc_1_pc, uc_1_r_w_0, uc_1_ram, uc_1_rst_pc, ula_1_overflow, ula_1_zero;
  wire [2:0] uc_1_opcode;
  wire [3:0] ac_1_q, counter_1_q, mux_1_s, ram_1_data, uc_1_dado, uc_1_operando, ula_1_s;
  wire [7:0] ir_1_q, rom_1_data;

  Counter #(.width(4), .max('hf)) counter_1 (
    .load(uc_1_load), .D(uc_1_dado), .count(not_1_out), .Q(counter_1_q), .clk(uc_1_pc), .clr(uc_1_rst_pc));  // open: carry
  not not_1 (not_1_out, uc_1_load);
  UC uc_1 (
    .OPERANDO(uc_1_operando), .E(uc_1_e), .OPCODE(uc_1_opcode), .\INSTRUÇÃO (ir_1_q), .Clock(clock_1_out),
    .IR(uc_1_ir), .PC(uc_1_pc), .AC(uc_1_ac), .RAM(uc_1_ram), .in_3(Reset_out), .RST_PC(uc_1_rst_pc),
    .R_W_0(uc_1_r_w_0), .Overflow(Overflow_q), .Zero(d_ff_1_q), .Load(uc_1_load), .Dado(uc_1_dado));
  Clock clock_1 (.out(clock_1_out));
  Button Reset (.out(Reset_out));
  // Probe on rom_1_data
  ROM #(.addrWidth(4)) rom_1 (.addr(counter_1_q), .data(rom_1_data));  // open: sel
  IR ir_1 (.Clock(uc_1_ir), .Q(ir_1_q), .E(rom_1_data));
  // Probe on ir_1_q
  // Probe on uc_1_operando
  // Probe on ac_1_q
  // Probe on uc_1_opcode
  MUX mux_1 (.Controle(uc_1_e), .A(uc_1_operando), .B(ram_1_data), .S(mux_1_s));
  // Probe on mux_1_s
  ULA ula_1 (
    .D(uc_1_e), .B(mux_1_s), .A(ac_1_q), .Overflow(ula_1_overflow), .Zero(ula_1_zero),
    .Controle(uc_1_opcode), .S(ula_1_s));
  // Probe on ula_1_s
  AC ac_1 (.in_1(uc_1_ac), .D(ula_1_s), .Q(ac_1_q));
  RAM #(.addrWidth(4), .dataWidth(4)) ram_1 (
    .addr(uc_1_operando), .data(ram_1_data), .clk(uc_1_ram), .ld(uc_1_r_w_0));  // open: sel, clr
  D_Flip_Flop Overflow (.clk(uc_1_ac), .D(ula_1_overflow), .Q(Overflow_q));  // open: Qn, preset, en, reset
  D_Flip_Flop d_ff_1 (.clk(uc_1_ac), .D(ula_1_zero), .Q(d_ff_1_q));  // open: Qn, preset, en, reset
  not not_2 (not_2_out, uc_1_r_w_0);
  Buffer buffer_1 (.B(ac_1_q), .C(not_2_out), .S(ram_1_data));

  // Notes on the sheet:
  //   3
  //   4
  //   5
  //   7
  //   8
  //   C
  //   F
  //   0
  //   0
  //   MOV
  //   000
  //   1
  //   000
  //   1
  //   MOV
  //   0
  //   2
  //   ADD
  //   001
  //   1
  //   001
  //   ADD
  //   0
  //   010
  //   SUB
  //   1
  //   010
  //   SUB
  //   0
  //   6
  //   OR
  //   011
  //   1
  //   OR
  //   011
  //   0
  //   NOT
  //   100
  //   100
  //   NOT
  //   1
  //   9
  //   101
  //   0
  //   A
  //   SHF
  //   1
  //   101
  //   B
  //   SHF
  //   0
  //   JPZ
  //   110
  //   JPO
  //   110
  //   1
  //   D
  //   GO
  //   111
  //   0
  //   E
  //   STR
  //   1
  //   111
  //   Instruction Set
  //   AC <= X
  //   AC <= M(X)
  //   AC <= AC+X
  //   AC <= AC+M(X)
  //   AC <= AC-X
  //   AC <= AC-M(X)
  //   AC <= AC OR X
  //   AC <= AC OR M(X)
  //   AC <= NOT X
  //   AC <= NOT M( X)
  //   AC <= AC << Q
  //   AC <= AC >> Q
  //   PC <= X SE FLAG Z
  //   PC <= X SE FLAG O
  //   PC <= X
  //   M(X) <= AC 
  //   PROCESSADOR RISC 4 BITS - SI4N - 2025-2
  //   Memória de Programa
  //   PC
  //   contents of rom_1 (hex, n*v repeats v):
  //   0 c0 f0 e1 f0 21 f0 21 f0 21 f0 21 f0 21 f0 f0
  //   Memória de Dados
endmodule

module Add_1 (
  input  A,
  input  B,
  input  Vem_1,
  output Soma,
  output Vai_1
);

  wire and_1_out, and_2_out, and_3_out, and_4_out, and_5_out, and_6_out, and_7_out, not_1_out, not_2_out,
       not_3_out, not_4_out, not_5_out, not_6_out;

  not not_1 (not_1_out, A);
  not not_2 (not_2_out, B);
  not not_3 (not_3_out, A);
  not not_4 (not_4_out, Vem_1);
  not not_5 (not_5_out, B);
  not not_6 (not_6_out, Vem_1);
  and and_1 (and_1_out, B, Vem_1);
  and and_2 (and_2_out, A, Vem_1);
  and and_3 (and_3_out, A, B);
  and and_4 (and_4_out, not_1_out, not_2_out, Vem_1);
  and and_5 (and_5_out, not_3_out, B, not_4_out);
  and and_6 (and_6_out, A, not_5_out, not_6_out);
  and and_7 (and_7_out, A, B, Vem_1);
  or or_1 (Vai_1, and_1_out, and_2_out, and_3_out);
  or or_2 (Soma, and_4_out, and_5_out, and_6_out, and_7_out);
endmodule

module Add_4 (
  input  [3:0] B,
  input  [3:0] A,
  output out_3,
  output [3:0] S
);

  wire add_1_2_vai_1, add_1_3_vai_1, add_1_4_vai_1;

  // Probe on A
  Add_1 add_1_1 (.A(A[3]), .B(B[3]), .Vem_1(add_1_2_vai_1), .Soma(S[3]), .Vai_1(out_3));
  Add_1 add_1_2 (.A(A[2]), .B(B[2]), .Vem_1(add_1_3_vai_1), .Soma(S[2]), .Vai_1(add_1_2_vai_1));
  Add_1 add_1_3 (.A(A[1]), .B(B[1]), .Vem_1(add_1_4_vai_1), .Soma(S[1]), .Vai_1(add_1_3_vai_1));
  Add_1 add_1_4 (.A(A[0]), .B(B[0]), .Vem_1(1'b0), .Soma(S[0]), .Vai_1(add_1_4_vai_1));
endmodule

module OR_4 (
  input  [3:0] B,
  input  [3:0] A,
  output [3:0] S
);

  or or_1 (S[3], A[3], B[3]);
  or or_2 (S[2], A[2], B[2]);
  or or_3 (S[0], A[0], B[0]);
  or or_4 (S[1], A[1], B[1]);
endmodule

module NOT (
  input  [3:0] B,
  output [3:0] S
);

  not not_1 (S[3], B[3]);
  not not_2 (S[2], B[2]);
  not not_3 (S[0], B[0]);
  not not_4 (S[1], B[1]);
endmodule

module Buffer (
  input  [3:0] B,
  input  C,
  output [3:0] S
);

  assign S[2] = C ? B[2] : 1'bz;  // Controlled_Buffer controlled_buffer_1
  assign S[3] = C ? B[3] : 1'bz;  // Controlled_Buffer controlled_buffer_2
  assign S[1] = C ? B[1] : 1'bz;  // Controlled_Buffer controlled_buffer_3
  assign S[0] = C ? B[0] : 1'bz;  // Controlled_Buffer controlled_buffer_4
endmodule

module Dec_3x8 (
  input  [2:0] in_1,
  output a,
  output b,
  output c,
  output d,
  output e,
  output f,
  output g,
  output h
);

  wire not_1_out, not_2_out, not_3_out, not_4_out, not_5_out, not_6_out, not_7_out, not_8_out, not_9_out,
       not_10_out, not_11_out, not_12_out;

  not not_1 (not_1_out, in_1[2]);
  not not_2 (not_2_out, in_1[1]);
  not not_3 (not_3_out, in_1[0]);
  not not_4 (not_4_out, in_1[2]);
  not not_5 (not_5_out, in_1[1]);
  not not_6 (not_6_out, in_1[2]);
  not not_7 (not_7_out, in_1[0]);
  not not_8 (not_8_out, in_1[2]);
  not not_9 (not_9_out, in_1[1]);
  not not_10 (not_10_out, in_1[0]);
  not not_11 (not_11_out, in_1[1]);
  not not_12 (not_12_out, in_1[0]);
  and and_1 (h, in_1[2], in_1[1], in_1[0]);
  and and_2 (a, not_1_out, not_2_out, not_3_out);
  and and_3 (b, not_4_out, not_5_out, in_1[0]);
  and and_4 (c, not_6_out, in_1[1], not_7_out);
  and and_5 (d, not_8_out, in_1[1], in_1[0]);
  and and_6 (e, in_1[2], not_9_out, not_10_out);
  and and_7 (f, in_1[2], not_11_out, in_1[0]);
  and and_8 (g, in_1[2], in_1[1], not_12_out);
endmodule

module Rot_e (
  input  [3:0] abcd,
  input  [1:0] xy,
  output [3:0] ABCD_2
);

  wire and_1_out, and_2_out, and_3_out, and_4_out, and_5_out, and_6_out, and_7_out, and_8_out, and_9_out;

  and and_1 (and_1_out, ~xy[1], ~xy[0], abcd[3]);  // AND_Gate
  and and_2 (and_2_out, ~xy[1], xy[0], abcd[2]);  // AND_Gate
  and and_3 (and_3_out, xy[1], ~xy[0], abcd[1]);  // AND_Gate
  and and_4 (and_4_out, xy[1], xy[0], abcd[0]);
  and and_5 (and_5_out, ~xy[1], ~xy[0], abcd[2]);  // AND_Gate
  and and_6 (and_6_out, ~xy[1], xy[0], abcd[1]);  // AND_Gate
  and and_7 (and_7_out, xy[1], ~xy[0], abcd[0]);  // AND_Gate
  and and_8 (and_8_out, ~xy[1], ~xy[0], abcd[1]);  // AND_Gate
  or or_1 (ABCD_2[1], and_8_out, and_9_out);
  and and_9 (and_9_out, ~xy[1], xy[0], abcd[0]);  // AND_Gate
  and and_10 (ABCD_2[0], ~xy[1], ~xy[0], abcd[0]);  // AND_Gate
  or or_2 (ABCD_2[3], and_1_out, and_2_out, and_3_out, and_4_out);
  or or_3 (ABCD_2[2], and_5_out, and_6_out, and_7_out);
endmodule

module Rot_d (
  input  [3:0] abcd,
  input  [1:0] xy,
  output [3:0] ABCD_2
);

  wire and_1_out, and_2_out, and_3_out, and_4_out, and_5_out, and_6_out, and_7_out, and_8_out, and_9_out;

  and and_1 (and_1_out, ~xy[1], ~xy[0], abcd[0]);  // AND_Gate
  and and_2 (and_2_out, ~xy[1], xy[0], abcd[1]);  // AND_Gate
  and and_3 (and_3_out, xy[1], ~xy[0], abcd[2]);  // AND_Gate
  and and_4 (and_4_out, xy[1], xy[0], abcd[3]);
  and and_5 (and_5_out, ~xy[1], ~xy[0], abcd[1]);  // AND_Gate
  and and_6 (and_6_out, ~xy[1], xy[0], abcd[2]);  // AND_Gate
  and and_7 (and_7_out, xy[1], ~xy[0], abcd[3]);  // AND_Gate
  and and_8 (and_8_out, ~xy[1], ~xy[0], abcd[2]);  // AND_Gate
  or or_1 (ABCD_2[2], and_8_out, and_9_out);
  and and_9 (and_9_out, ~xy[1], xy[0], abcd[3]);  // AND_Gate
  and and_10 (ABCD_2[3], ~xy[1], ~xy[0], abcd[3]);  // AND_Gate
  or or_2 (ABCD_2[0], and_1_out, and_2_out, and_3_out, and_4_out);
  or or_3 (ABCD_2[1], and_5_out, and_6_out, and_7_out);
endmodule

module Sub_1 (
  input  A,
  input  B,
  input  VEM_1,
  output S,
  output VAI_1
);

  wire and_1_out, and_2_out, and_3_out, and_4_out, and_5_out, and_6_out, and_7_out, not_1_out, not_2_out,
       not_3_out, not_4_out, not_5_out, not_6_out, not_7_out, not_8_out;

  not not_1 (not_1_out, A);
  not not_2 (not_2_out, B);
  not not_3 (not_3_out, A);
  not not_4 (not_4_out, VEM_1);
  not not_5 (not_5_out, B);
  not not_6 (not_6_out, VEM_1);
  not not_7 (not_7_out, A);
  not not_8 (not_8_out, A);
  and and_1 (and_1_out, not_1_out, not_2_out, VEM_1);
  and and_2 (and_2_out, not_3_out, B, not_4_out);
  and and_3 (and_3_out, A, not_5_out, not_6_out);
  and and_4 (and_4_out, A, B, VEM_1);
  and and_5 (and_5_out, not_7_out, VEM_1);
  and and_6 (and_6_out, not_8_out, B);
  and and_7 (and_7_out, B, VEM_1);
  or or_1 (S, and_1_out, and_2_out, and_3_out, and_4_out);
  or or_2 (VAI_1, and_5_out, and_6_out, and_7_out);
endmodule

module Sub_4 (
  input  [3:0] B,
  input  [3:0] A,
  output out_3,
  output [3:0] S
);

  wire sub_1_2_vai_1, sub_1_3_vai_1, sub_1_4_vai_1;

  // Probe on A
  Sub_1 sub_1_1 (.A(A[3]), .B(B[3]), .VEM_1(sub_1_2_vai_1), .S(S[3]), .VAI_1(out_3));
  Sub_1 sub_1_2 (.A(A[2]), .B(B[2]), .VEM_1(sub_1_3_vai_1), .S(S[2]), .VAI_1(sub_1_2_vai_1));
  Sub_1 sub_1_3 (.A(A[1]), .B(B[1]), .VEM_1(sub_1_4_vai_1), .S(S[1]), .VAI_1(sub_1_3_vai_1));
  Sub_1 sub_1_4 (.A(A[0]), .B(B[0]), .VEM_1(1'b0), .S(S[0]), .VAI_1(sub_1_4_vai_1));
endmodule

module ULA (
  input  D,
  input  [3:0] B,
  input  [3:0] A,
  input  [2:0] Controle,
  output Overflow,
  output [3:0] S,
  output Zero
);

  wire add_4_1_out_3, and_1_out, and_2_out, dec_3x8_1_a, dec_3x8_1_b, dec_3x8_1_c, dec_3x8_1_d, dec_3x8_1_e,
       dec_3x8_1_f, dec_3x8_1_g, dec_3x8_1_h, not_2_out, sub_4_1_out_3;
  wire [3:0] add_4_1_s, buffer_6_s, not_1_s, or_4_1_s, rot_d_1_abcd_2, rot_e_1_abcd_2, sub_4_1_s;

  or or_1 (Overflow, and_1_out, and_2_out);
  and and_1 (and_1_out, add_4_1_out_3, dec_3x8_1_b);
  and and_2 (and_2_out, sub_4_1_out_3, dec_3x8_1_c);
  Dec_3x8 dec_3x8_1 (
    .a(dec_3x8_1_a), .b(dec_3x8_1_b), .c(dec_3x8_1_c), .d(dec_3x8_1_d), .e(dec_3x8_1_e), .f(dec_3x8_1_f),
    .g(dec_3x8_1_g), .h(dec_3x8_1_h), .in_1(Controle));
  Buffer buffer_1 (.B(B), .C(dec_3x8_1_a), .S(S));
  Add_4 add_4_1 (.A(A), .out_3(add_4_1_out_3), .B(B), .S(add_4_1_s));
  Buffer buffer_2 (.B(add_4_1_s), .C(dec_3x8_1_b), .S(S));
  Sub_4 sub_4_1 (.A(A), .out_3(sub_4_1_out_3), .B(B), .S(sub_4_1_s));
  Buffer buffer_3 (.B(sub_4_1_s), .C(dec_3x8_1_c), .S(S));
  and and_3 (Zero, ~S[0], ~S[1], ~S[2], ~S[3], ~dec_3x8_1_g, ~dec_3x8_1_h);  // AND_Gate
  OR_4 or_4_1 (.A(A), .B(B), .S(or_4_1_s));
  NOT not_1 (.B(B), .S(not_1_s));
  Buffer buffer_4 (.B(or_4_1_s), .C(dec_3x8_1_d), .S(S));
  Buffer buffer_5 (.B(not_1_s), .C(dec_3x8_1_e), .S(S));
  Rot_e rot_e_1 (.ABCD_2(rot_e_1_abcd_2), .abcd(A), .xy(B[1:0]));
  Rot_d rot_d_1 (.ABCD_2(rot_d_1_abcd_2), .abcd(A), .xy(B[1:0]));
  Buffer buffer_6 (.B(rot_e_1_abcd_2), .C(not_2_out), .S(buffer_6_s));
  not not_2 (not_2_out, D);
  Buffer buffer_7 (.B(rot_d_1_abcd_2), .C(D), .S(buffer_6_s));
  Buffer buffer_8 (.B(buffer_6_s), .C(dec_3x8_1_f), .S(S));
endmodule

module AC (
  input  in_1,
  input  [3:0] D,
  output [3:0] Q
);

  D_Flip_Flop d_ff_1 (.clk(in_1), .D(D[2]), .Q(Q[2]));  // open: Qn, preset, en, reset
  D_Flip_Flop d_ff_2 (.clk(in_1), .D(D[3]), .Q(Q[3]));  // open: Qn, preset, en, reset
  D_Flip_Flop d_ff_3 (.clk(in_1), .D(D[1]), .Q(Q[1]));  // open: Qn, preset, en, reset
  D_Flip_Flop d_ff_4 (.clk(in_1), .D(D[0]), .Q(Q[0]));  // open: Qn, preset, en, reset
endmodule

module MUX (
  input  [3:0] A,
  input  [3:0] B,
  input  Controle,
  output [3:0] S
);

  wire not_1_out;

  Buffer buffer_1 (.B(A), .C(not_1_out), .S(S));
  not not_1 (not_1_out, Controle);
  Buffer buffer_2 (.B(B), .C(Controle), .S(S));
endmodule

module IR (
  input  Clock,
  input  [7:0] E,
  output [7:0] Q
);

  D_Flip_Flop #(.trigger("falling")) D7 (.clk(Clock), .D(E[7]), .Q(Q[7]));  // open: Qn, preset, en, reset
  D_Flip_Flop #(.trigger("falling")) D6 (.clk(Clock), .D(E[6]), .Q(Q[6]));  // open: Qn, preset, en, reset
  D_Flip_Flop #(.trigger("falling")) D5 (.clk(Clock), .D(E[5]), .Q(Q[5]));  // open: Qn, preset, en, reset
  D_Flip_Flop #(.trigger("falling")) D4 (.clk(Clock), .D(E[4]), .Q(Q[4]));  // open: Qn, preset, en, reset
  D_Flip_Flop #(.trigger("falling")) D3 (.clk(Clock), .D(E[3]), .Q(Q[3]));  // open: Qn, preset, en, reset
  D_Flip_Flop #(.trigger("falling")) D2 (.clk(Clock), .D(E[2]), .Q(Q[2]));  // open: Qn, preset, en, reset
  D_Flip_Flop #(.trigger("falling")) D1 (.clk(Clock), .D(E[1]), .Q(Q[1]));  // open: Qn, preset, en, reset
  D_Flip_Flop #(.trigger("falling")) D0 (.clk(Clock), .D(E[0]), .Q(Q[0]));  // open: Qn, preset, en, reset
endmodule

module UC (
  input  Clock,
  input  [7:0] \INSTRUÇÃO ,
  input  in_3,
  input  Overflow,
  input  Zero,
  output IR,
  output AC,
  output RAM,
  output RST_PC,
  output PC,
  output [3:0] Dado,
  output [3:0] OPERANDO,
  output E,
  output [2:0] OPCODE,
  output R_W_0,
  output Load
);

  wire GOTO_out, JO_out, JZ_out;
  wire [1:0] counter_1_q;

  Counter #(.width(2), .max('h3)) counter_1 (.Q(counter_1_q), .clk(Clock), .clr(in_3));  // open: load, D, count, carry
  and and_1 (IR, ~counter_1_q[1], ~counter_1_q[0]);  // AND_Gate
  or or_1 (Load, JZ_out, JO_out, GOTO_out);
  and and_2 (PC, ~counter_1_q[1], counter_1_q[0]);  // AND_Gate
  and and_3 (RAM, counter_1_q[1], counter_1_q[0]);
  and and_4 (AC, counter_1_q[1], ~counter_1_q[0]);  // AND_Gate
  and JZ (JZ_out, Zero, PC, \INSTRUÇÃO [7], \INSTRUÇÃO [6], ~\INSTRUÇÃO [5], ~\INSTRUÇÃO [4]);  // AND_Gate
  and JO (JO_out, Overflow, PC, \INSTRUÇÃO [7], \INSTRUÇÃO [6], ~\INSTRUÇÃO [5], \INSTRUÇÃO [4]);  // AND_Gate
  and GOTO (GOTO_out, PC, \INSTRUÇÃO [7], \INSTRUÇÃO [6], \INSTRUÇÃO [5], ~\INSTRUÇÃO [4]);  // AND_Gate
  nand R_W (R_W_0, AC, \INSTRUÇÃO [7], \INSTRUÇÃO [6], \INSTRUÇÃO [5], \INSTRUÇÃO [4]);

  assign Dado = \INSTRUÇÃO [3:0];
  assign E = \INSTRUÇÃO [4];
  assign OPCODE = \INSTRUÇÃO [7:5];
  assign OPERANDO = \INSTRUÇÃO [3:0];
  assign RST_PC = in_3;
endmodule
